# Fritzing sketch 流水灯 (saved by Fritzing 0.9.3b)
breadboards: 1

parts:
  元件1 = Arduino Uno (Rev3)
  S1 = Momentary Switch [package=ksa_sealed_tac_switch]
  R1 = Resistor [tolerance=±5% resistance=1k package=THT]

nets:
  N1: 元件1.GND, R1.Pin_0
  N2: 元件1.D7, R1.Pin_1
  N3: S1.1, S1.2
  N4: S1.3, S1.4
